# Fritzing sketch Hypatia_TempRelhLogger_Extended_1 (saved by Fritzing 0.9.3b)
breadboards: 1

parts:
  Part1 = Adafruit Feather M0 Adalogger [part_number="Adafruit #2796"]
  RHT2 = Humidity and Temperature Sensor RHT03 [part_number=DHT22]
  U1 = SWITCH_SPDT [package=kps-1290]

nets:
  N1: Part1.GND, RHT2.GND_2, U1.P
  +3V3: Part1.+3V3, RHT2.Vcc
  N2: Part1.D12, U1.S
  N3: Part1.D6, RHT2.Data-signal

custom parts:
  Adafruit Feather M0 Adalogger: This is the Adafruit Feather M0 Adalogger - our take on an 'all-in-one' Cortex M0 datalogger (or data-reader) with built in USB and battery charging. Its an Adafruit Feather M0 with a microSD holder ready to rock! We have other boards in the Feather family, check'em out here At the Feather M0's heart is an ATSAMD21G18 ARM Cortex M0 processor, clocked at 48 MHz and at 3.3V logic, the same one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
